// Logisim project ALU.circ as structural Verilog: 2 circuits, main circuit main
module main (
  input  [31:0] a,
  input  [31:0] b,
  input  [3:0] aluop,
  input  output_inverted,
  input  output_inc,
  input  clk,
  input  rst,
  output [31:0] res_low,
  output [31:0] res_high,
  output done
);

  wire [4:0] clo_1_cnt, clz_1_cnt;
  wire [31:0] divisor_1_quotient, divisor_1_remainder, multiplexer_3_out, multiplexer_4_out;
  wire [63:0] adder_1_out, adder_2_out, and_1_out, bit_extender_1_out, bit_extender_2_out, multiplexer_1_out,
       multiplexer_2_out, not_1_out, or_1_out, rotr_1_res, s_l_l_1_res, s_r_a_1_res, s_r_l_1_res,
       subtractor_1_out, xor_1_out;

  assign bit_extender_1_out = {{32{1'b0}}, a};  // Bit_Extender bit_extender_1
  assign bit_extender_2_out = {{32{1'b0}}, b};  // Bit_Extender bit_extender_2
  Adder #(.width(64)) adder_1 (.a(bit_extender_1_out), .b(bit_extender_2_out), .out(adder_1_out));  // open: cin, cout
  Subtractor #(.width(64)) subtractor_1 (
    .a(bit_extender_1_out), .b(bit_extender_2_out), .out(subtractor_1_out));  // open: bin, bout
  assign and_1_out = bit_extender_1_out & bit_extender_2_out;  // AND_Gate and_1, 64 bits wide
  assign or_1_out = bit_extender_1_out | bit_extender_2_out;  // OR_Gate or_1, 64 bits wide
  assign xor_1_out = bit_extender_1_out ^ bit_extender_2_out;  // XOR_Gate xor_1, 64 bits wide
  divisor divisor_1 (
    .divisor(b), .dividend(a), .start(rst), .clk(clk), .quotient(divisor_1_quotient),
    .remainder(divisor_1_remainder), .done(done));
  CLO clo_1 (.in1(a), .S(1'b1), .clk(clk), .En(1'b1), .rst(rst), .cnt(clo_1_cnt));  // open: D
  CLZ clz_1 (.in1(a), .S(1'b1), .clk(clk), .En(1'b1), .rst(rst), .cnt(clz_1_cnt));  // open: D
  S_L_L s_l_l_1 (.A(a), .shamt(b[4:0]), .res(s_l_l_1_res));
  S_R_L s_r_l_1 (.A(a), .shamt(b[4:0]), .res(s_r_l_1_res));
  S_R_A s_r_a_1 (.A(a), .shamt(b[4:0]), .res(s_r_a_1_res));
  ROTR rotr_1 (.A(a), .shamt(b[4:0]), .res(rotr_1_res));
  Multiplexer #(.select(4), .width(64)) multiplexer_1 (
    .in0(adder_1_out), .in1(subtractor_1_out), .in3({divisor_1_remainder, divisor_1_quotient}),
    .in4(and_1_out), .in5(or_1_out), .in6(xor_1_out), .in7({{59{1'b0}}, clo_1_cnt}),
    .in8({{59{1'b0}}, clz_1_cnt}), .in9(s_l_l_1_res), .in10(s_r_l_1_res), .in11(s_r_a_1_res),
    .in12(rotr_1_res), .out(multiplexer_1_out), .sel(aluop));  // open: in2, in13, in14, in15
  assign not_1_out = ~multiplexer_1_out;  // NOT_Gate not_1, 64 bits wide
  Multiplexer #(.width(64)) multiplexer_2 (
    .in0(multiplexer_1_out), .in1(not_1_out), .out(multiplexer_2_out), .sel(output_inverted));
  Adder #(.width(64)) adder_2 (
    .a(multiplexer_2_out), .b({64{1'b0}}), .out(adder_2_out), .cin(output_inc));  // open: cout
  Multiplexer #(.width(32)) multiplexer_3 (.in0(adder_2_out[31:0]), .out(multiplexer_3_out), .sel(rst));  // open: in1
  Multiplexer #(.width(32)) multiplexer_4 (.in0(adder_2_out[63:32]), .out(multiplexer_4_out), .sel(rst));  // open: in1
  Register #(.width(32)) register_1 (.D(multiplexer_3_out), .clk(clk), .Q(res_low), .clr(rst));  // open: en
  Register #(.width(32)) register_2 (.D(multiplexer_4_out), .clk(clk), .Q(res_high), .clr(rst));  // open: en

  // Notes on the sheet:
  //   a: initial=0x5d9d70bb
  //   b: initial=0x6466e6c8
  //   aluop: initial=0x9
endmodule

module divisor (
  input  [31:0] divisor,
  input  [31:0] dividend,
  input  start,
  input  clk,
  output [31:0] quotient,
  output [31:0] remainder,
  output done
);

  wire and_1_out, bitselector_1_out, comparator_1_eq, comparator_2_lt, not_1_out, not_2_out;
  wire [6:0] counter_q, multiplexer_4_out, multiplexer_8_out, subtractor_1_out;
  wire [31:0] A_q, adder_1_out, B_q, bit_extender_1_out, multiplexer_1_out, multiplexer_2_out,
       multiplexer_3_out, multiplexer_5_out, multiplexer_6_out, multiplexer_7_out, multiplexer_9_out,
       multiplexer_10_out, or_1_out, Q_q, shifter_1_out, shifter_2_out, subtractor_2_out;

  Multiplexer #(.width(32)) multiplexer_1 (
    .in0(multiplexer_9_out), .in1({32{1'b0}}), .out(multiplexer_1_out), .sel(start));
  Multiplexer #(.width(32)) multiplexer_2 (.in0(B_q), .in1(divisor), .out(multiplexer_2_out), .sel(start));
  Multiplexer #(.width(32)) multiplexer_3 (
    .in0(multiplexer_10_out), .in1(dividend), .out(multiplexer_3_out), .sel(start));
  Multiplexer #(.width(7)) multiplexer_4 (
    .in0(multiplexer_8_out), .in1(7'b0110000), .out(multiplexer_4_out), .sel(start));
  Subtractor #(.width(7)) subtractor_1 (.a(counter_q), .b(7'b0000001), .out(subtractor_1_out));  // open: bin, bout
  Multiplexer #(.width(32)) multiplexer_5 (.in0(multiplexer_1_out), .in1(A_q), .out(multiplexer_5_out), .sel(done));
  Multiplexer #(.width(32)) multiplexer_6 (.in0(multiplexer_2_out), .in1(B_q), .out(multiplexer_6_out), .sel(done));
  Multiplexer #(.width(32)) multiplexer_7 (.in0(multiplexer_3_out), .in1(Q_q), .out(multiplexer_7_out), .sel(done));
  Register #(.width(32)) A (.D(multiplexer_5_out), .en(1'b1), .clk(clk), .Q(A_q));  // open: clr
  Register #(.width(32)) B (.D(multiplexer_6_out), .en(1'b1), .clk(clk), .Q(B_q));  // open: clr
  Register #(.width(32)) Q (.D(multiplexer_7_out), .en(1'b1), .clk(clk), .Q(Q_q));  // open: clr
  Register #(.width(7)) counter (.D(multiplexer_4_out), .en(1'b1), .clk(clk), .Q(counter_q));  // open: clr
  Shifter #(.width(32)) shifter_1 (.in(A_q), .\dist (5'b00001), .out(shifter_1_out));
  BitSelector #(.width(32)) bitselector_1 (.in(Q_q), .out(bitselector_1_out), .sel({5{1'b1}}));
  Comparator #(.width(7)) comparator_1 (.a(counter_q), .b({7{1'b0}}), .eq(comparator_1_eq));  // open: gt, lt
  assign bit_extender_1_out = {{31{1'b0}}, bitselector_1_out};  // Bit_Extender bit_extender_1
  Adder #(.width(32)) adder_1 (.a(shifter_1_out), .b(bit_extender_1_out), .out(adder_1_out));  // open: cin, cout
  Shifter #(.width(32)) shifter_2 (.in(Q_q), .\dist (5'b00001), .out(shifter_2_out));
  Multiplexer #(.width(7)) multiplexer_8 (
    .in0(subtractor_1_out), .in1(counter_q), .out(multiplexer_8_out), .sel(comparator_1_eq));
  Subtractor #(.width(32)) subtractor_2 (.a(adder_1_out), .b(B_q), .out(subtractor_2_out));  // open: bin, bout
  Comparator #(.width(32)) comparator_2 (.a(adder_1_out), .b(B_q), .lt(comparator_2_lt));  // open: gt, eq
  not not_1 (not_1_out, comparator_2_lt);
  assign or_1_out = shifter_2_out | 32'h1;  // OR_Gate or_1, 32 bits wide
  and and_1 (and_1_out, comparator_1_eq, not_2_out);
  not not_2 (not_2_out, start);
  Multiplexer #(.width(32)) multiplexer_9 (
    .in0(adder_1_out), .in1(subtractor_2_out), .out(multiplexer_9_out), .sel(not_1_out));
  Multiplexer #(.width(32)) multiplexer_10 (
    .in0(shifter_2_out), .in1(or_1_out), .out(multiplexer_10_out), .sel(not_1_out));
  Multiplexer #(.width(32)) multiplexer_11 (.in1(Q_q), .out(quotient), .sel(and_1_out));  // open: in0
  Multiplexer #(.width(32)) multiplexer_12 (.in1(A_q), .out(remainder), .sel(and_1_out));  // open: in0
  Multiplexer multiplexer_13 (.in0(1'b0), .in1(1'b1), .out(done), .sel(and_1_out));

  // Notes on the sheet:
  //   divisor: initial=0xf
  //   dividend: initial=0x8
  //   clk: initial=0x1
endmodule
